// Logisim project Mini MIPS Processor.circ as structural Verilog: 6 circuits, main circuit Combined Circuit
module REG_FILE (
  input  [5:0] Read_Reg_1,
  input  [25:0] Write_Data,
  input  CLK,
  input  [5:0] Right_Reg_RD,
  input  Write_Control,
  input  [5:0] Read_Reg_2,
  output [25:0] Read_Data_1,
  output [25:0] Read_Data_2
);

  wire decoder_1_out0, decoder_1_out1, decoder_2_out0, decoder_2_out1, decoder_2_out2, decoder_2_out3,
       decoder_2_out4, decoder_2_out5, decoder_2_out6, decoder_2_out7, decoder_2_out8, decoder_2_out9,
       decoder_2_out10, decoder_2_out11, decoder_2_out12, decoder_2_out13, decoder_2_out14, decoder_2_out15,
       decoder_2_out16, decoder_2_out17, decoder_2_out18, decoder_2_out19, decoder_2_out20, decoder_2_out21,
       decoder_2_out22, decoder_2_out23, decoder_2_out24, decoder_2_out25, decoder_2_out26, decoder_2_out27,
       decoder_2_out28, decoder_2_out29, decoder_2_out30, decoder_2_out31, decoder_3_out0, decoder_3_out1,
       decoder_3_out2, decoder_3_out3, decoder_3_out4, decoder_3_out5, decoder_3_out6, decoder_3_out7,
       decoder_3_out8, decoder_3_out9, decoder_3_out10, decoder_3_out11, decoder_3_out12, decoder_3_out13,
       decoder_3_out14, decoder_3_out15, decoder_3_out16, decoder_3_out17, decoder_3_out18, decoder_3_out19,
       decoder_3_out20, decoder_3_out21, decoder_3_out22, decoder_3_out23, decoder_3_out24, decoder_3_out25,
       decoder_3_out26, decoder_3_out27, decoder_3_out28, decoder_3_out29, decoder_3_out30, decoder_3_out31;
  wire [25:0] multiplexer_1_out, multiplexer_2_out, multiplexer_3_out, multiplexer_4_out, register_1_q,
       register_2_q, register_3_q, register_4_q, register_5_q, register_6_q, register_7_q, register_8_q,
       register_9_q, register_10_q, register_11_q, register_12_q, register_13_q, register_14_q,
       register_15_q, register_16_q, register_17_q, register_18_q, register_19_q, register_20_q,
       register_21_q, register_22_q, register_23_q, register_24_q, register_25_q, register_26_q,
       register_27_q, register_28_q, register_29_q, register_30_q, register_31_q, register_32_q,
       register_33_q, register_34_q, register_35_q, register_36_q, register_37_q, register_38_q,
       register_39_q, register_40_q, register_41_q, register_42_q, register_43_q, register_44_q,
       register_45_q, register_46_q, register_47_q, register_48_q, register_49_q, register_50_q,
       register_51_q, register_52_q, register_53_q, register_54_q, register_55_q, register_56_q,
       register_57_q, register_58_q, register_59_q, register_60_q, register_61_q, register_62_q,
       register_63_q, register_64_q;

  Decoder #(.disabled(0)) decoder_1 (
    .out0(decoder_1_out0), .out1(decoder_1_out1), .sel(Right_Reg_RD[5]), .en(Write_Control));
  Decoder #(.select(5), .disabled(0)) decoder_2 (
    .out0(decoder_2_out0), .out1(decoder_2_out1), .out2(decoder_2_out2), .out3(decoder_2_out3),
    .out4(decoder_2_out4), .out5(decoder_2_out5), .out6(decoder_2_out6), .out7(decoder_2_out7),
    .out8(decoder_2_out8), .out9(decoder_2_out9), .out10(decoder_2_out10), .out11(decoder_2_out11),
    .out12(decoder_2_out12), .out13(decoder_2_out13), .out14(decoder_2_out14), .out15(decoder_2_out15),
    .out16(decoder_2_out16), .out17(decoder_2_out17), .out18(decoder_2_out18), .out19(decoder_2_out19),
    .out20(decoder_2_out20), .out21(decoder_2_out21), .out22(decoder_2_out22), .out23(decoder_2_out23),
    .out24(decoder_2_out24), .out25(decoder_2_out25), .out26(decoder_2_out26), .out27(decoder_2_out27),
    .out28(decoder_2_out28), .out29(decoder_2_out29), .out30(decoder_2_out30), .out31(decoder_2_out31),
    .sel(Right_Reg_RD[4:0]), .en(decoder_1_out0));
  Decoder #(.select(5), .disabled(0)) decoder_3 (
    .out0(decoder_3_out0), .out1(decoder_3_out1), .out2(decoder_3_out2), .out3(decoder_3_out3),
    .out4(decoder_3_out4), .out5(decoder_3_out5), .out6(decoder_3_out6), .out7(decoder_3_out7),
    .out8(decoder_3_out8), .out9(decoder_3_out9), .out10(decoder_3_out10), .out11(decoder_3_out11),
    .out12(decoder_3_out12), .out13(decoder_3_out13), .out14(decoder_3_out14), .out15(decoder_3_out15),
    .out16(decoder_3_out16), .out17(decoder_3_out17), .out18(decoder_3_out18), .out19(decoder_3_out19),
    .out20(decoder_3_out20), .out21(decoder_3_out21), .out22(decoder_3_out22), .out23(decoder_3_out23),
    .out24(decoder_3_out24), .out25(decoder_3_out25), .out26(decoder_3_out26), .out27(decoder_3_out27),
    .out28(decoder_3_out28), .out29(decoder_3_out29), .out30(decoder_3_out30), .out31(decoder_3_out31),
    .sel(Right_Reg_RD[4:0]), .en(decoder_1_out1));
  Register #(.width(26)) register_1 (.D(Write_Data), .en(decoder_2_out0), .Q(register_1_q), .clk(CLK));  // open: clr
  Register #(.width(26)) register_2 (.D(Write_Data), .en(decoder_2_out1), .Q(register_2_q), .clk(CLK));  // open: clr
  Register #(.width(26)) register_3 (.D(Write_Data), .en(decoder_2_out2), .Q(register_3_q), .clk(CLK));  // open: clr
  Register #(.width(26)) register_4 (.D(Write_Data), .en(decoder_2_out3), .Q(register_4_q), .clk(CLK));  // open: clr
  Register #(.width(26)) register_5 (.D(Write_Data), .en(decoder_2_out4), .Q(register_5_q), .clk(CLK));  // open: clr
  Register #(.width(26)) register_6 (.D(Write_Data), .en(decoder_2_out5), .Q(register_6_q), .clk(CLK));  // open: clr
  Register #(.width(26)) register_7 (.D(Write_Data), .en(decoder_2_out6), .Q(register_7_q), .clk(CLK));  // open: clr
  Register #(.width(26)) register_8 (.D(Write_Data), .en(decoder_2_out7), .Q(register_8_q), .clk(CLK));  // open: clr
  Register #(.width(26)) register_9 (.D(Write_Data), .en(decoder_2_out8), .Q(register_9_q), .clk(CLK));  // open: clr
  Register #(.width(26)) register_10 (.D(Write_Data), .en(decoder_2_out9), .Q(register_10_q), .clk(CLK));  // open: clr
  Register #(.width(26)) register_11 (.D(Write_Data), .en(decoder_2_out10), .Q(register_11_q), .clk(CLK));  // open: clr
  Register #(.width(26)) register_12 (.D(Write_Data), .en(decoder_2_out11), .Q(register_12_q), .clk(CLK));  // open: clr
  Register #(.width(26)) register_13 (.D(Write_Data), .en(decoder_2_out12), .Q(register_13_q), .clk(CLK));  // open: clr
  Register #(.width(26)) register_14 (.D(Write_Data), .en(decoder_2_out13), .Q(register_14_q), .clk(CLK));  // open: clr
  Register #(.width(26)) register_15 (.D(Write_Data), .en(decoder_2_out14), .Q(register_15_q), .clk(CLK));  // open: clr
  Register #(.width(26)) register_16 (.D(Write_Data), .en(decoder_2_out15), .Q(register_16_q), .clk(CLK));  // open: clr
  Register #(.width(26)) register_17 (.D(Write_Data), .en(decoder_2_out16), .Q(register_17_q), .clk(CLK));  // open: clr
  Register #(.width(26)) register_18 (.D(Write_Data), .en(decoder_2_out17), .Q(register_18_q), .clk(CLK));  // open: clr
  Register #(.width(26)) register_19 (.D(Write_Data), .en(decoder_2_out18), .Q(register_19_q), .clk(CLK));  // open: clr
  Register #(.width(26)) register_20 (.D(Write_Data), .en(decoder_2_out19), .Q(register_20_q), .clk(CLK));  // open: clr
  Register #(.width(26)) register_21 (.D(Write_Data), .en(decoder_2_out20), .Q(register_21_q), .clk(CLK));  // open: clr
  Register #(.width(26)) register_22 (.D(Write_Data), .en(decoder_2_out21), .Q(register_22_q), .clk(CLK));  // open: clr
  Register #(.width(26)) register_23 (.D(Write_Data), .en(decoder_2_out22), .Q(register_23_q), .clk(CLK));  // open: clr
  Register #(.width(26)) register_24 (.D(Write_Data), .en(decoder_2_out23), .Q(register_24_q), .clk(CLK));  // open: clr
  Register #(.width(26)) register_25 (.D(Write_Data), .en(decoder_2_out24), .Q(register_25_q), .clk(CLK));  // open: clr
  Register #(.width(26)) register_26 (.D(Write_Data), .en(decoder_2_out25), .Q(register_26_q), .clk(CLK));  // open: clr
  Register #(.width(26)) register_27 (.D(Write_Data), .en(decoder_2_out26), .Q(register_27_q), .clk(CLK));  // open: clr
  Register #(.width(26)) register_28 (.D(Write_Data), .en(decoder_2_out27), .Q(register_28_q), .clk(CLK));  // open: clr
  Register #(.width(26)) register_29 (.D(Write_Data), .en(decoder_2_out28), .Q(register_29_q), .clk(CLK));  // open: clr
  Register #(.width(26)) register_30 (.D(Write_Data), .en(decoder_2_out29), .Q(register_30_q), .clk(CLK));  // open: clr
  Register #(.width(26)) register_31 (.D(Write_Data), .en(decoder_2_out30), .Q(register_31_q), .clk(CLK));  // open: clr
  Register #(.width(26)) register_32 (.D(Write_Data), .en(decoder_2_out31), .Q(register_32_q), .clk(CLK));  // open: clr
  Register #(.width(26)) register_33 (.D(Write_Data), .en(decoder_3_out0), .Q(register_33_q), .clk(CLK));  // open: clr
  Register #(.width(26)) register_34 (.D(Write_Data), .en(decoder_3_out1), .Q(register_34_q), .clk(CLK));  // open: clr
  Register #(.width(26)) register_35 (.D(Write_Data), .en(decoder_3_out2), .Q(register_35_q), .clk(CLK));  // open: clr
  Register #(.width(26)) register_36 (.D(Write_Data), .en(decoder_3_out3), .Q(register_36_q), .clk(CLK));  // open: clr
  Register #(.width(26)) register_37 (.D(Write_Data), .en(decoder_3_out4), .Q(register_37_q), .clk(CLK));  // open: clr
  Register #(.width(26)) register_38 (.D(Write_Data), .en(decoder_3_out5), .Q(register_38_q), .clk(CLK));  // open: clr
  Register #(.width(26)) register_39 (.D(Write_Data), .en(decoder_3_out6), .Q(register_39_q), .clk(CLK));  // open: clr
  Register #(.width(26)) register_40 (.D(Write_Data), .en(decoder_3_out7), .Q(register_40_q), .clk(CLK));  // open: clr
  Register #(.width(26)) register_41 (.D(Write_Data), .en(decoder_3_out8), .Q(register_41_q), .clk(CLK));  // open: clr
  Register #(.width(26)) register_42 (.D(Write_Data), .en(decoder_3_out9), .Q(register_42_q), .clk(CLK));  // open: clr
  Register #(.width(26)) register_43 (.D(Write_Data), .en(decoder_3_out10), .Q(register_43_q), .clk(CLK));  // open: clr
  Register #(.width(26)) register_44 (.D(Write_Data), .en(decoder_3_out11), .Q(register_44_q), .clk(CLK));  // open: clr
  Register #(.width(26)) register_45 (.D(Write_Data), .en(decoder_3_out12), .Q(register_45_q), .clk(CLK));  // open: clr
  Register #(.width(26)) register_46 (.D(Write_Data), .en(decoder_3_out13), .Q(register_46_q), .clk(CLK));  // open: clr
  Register #(.width(26)) register_47 (.D(Write_Data), .en(decoder_3_out14), .Q(register_47_q), .clk(CLK));  // open: clr
  Register #(.width(26)) register_48 (.D(Write_Data), .en(decoder_3_out15), .Q(register_48_q), .clk(CLK));  // open: clr
  Register #(.width(26)) register_49 (.D(Write_Data), .en(decoder_3_out16), .Q(register_49_q), .clk(CLK));  // open: clr
  Register #(.width(26)) register_50 (.D(Write_Data), .en(decoder_3_out17), .Q(register_50_q), .clk(CLK));  // open: clr
  Register #(.width(26)) register_51 (.D(Write_Data), .en(decoder_3_out18), .Q(register_51_q), .clk(CLK));  // open: clr
  Register #(.width(26)) register_52 (.D(Write_Data), .en(decoder_3_out19), .Q(register_52_q), .clk(CLK));  // open: clr
  Register #(.width(26)) register_53 (.D(Write_Data), .en(decoder_3_out20), .Q(register_53_q), .clk(CLK));  // open: clr
  Register #(.width(26)) register_54 (.D(Write_Data), .en(decoder_3_out21), .Q(register_54_q), .clk(CLK));  // open: clr
  Register #(.width(26)) register_55 (.D(Write_Data), .en(decoder_3_out22), .Q(register_55_q), .clk(CLK));  // open: clr
  Register #(.width(26)) register_56 (.D(Write_Data), .en(decoder_3_out23), .Q(register_56_q), .clk(CLK));  // open: clr
  Register #(.width(26)) register_57 (.D(Write_Data), .en(decoder_3_out24), .Q(register_57_q), .clk(CLK));  // open: clr
  Register #(.width(26)) register_58 (.D(Write_Data), .en(decoder_3_out25), .Q(register_58_q), .clk(CLK));  // open: clr
  Register #(.width(26)) register_59 (.D(Write_Data), .en(decoder_3_out26), .Q(register_59_q), .clk(CLK));  // open: clr
  Register #(.width(26)) register_60 (.D(Write_Data), .en(decoder_3_out27), .Q(register_60_q), .clk(CLK));  // open: clr
  Register #(.width(26)) register_61 (.D(Write_Data), .en(decoder_3_out28), .Q(register_61_q), .clk(CLK));  // open: clr
  Register #(.width(26)) register_62 (.D(Write_Data), .en(decoder_3_out29), .Q(register_62_q), .clk(CLK));  // open: clr
  Register #(.width(26)) register_63 (.D(Write_Data), .en(decoder_3_out30), .Q(register_63_q), .clk(CLK));  // open: clr
  Register #(.width(26)) register_64 (.D(Write_Data), .en(decoder_3_out31), .Q(register_64_q), .clk(CLK));  // open: clr
  Multiplexer #(.select(5), .width(26)) multiplexer_1 (
    .in0(register_1_q), .in1(register_2_q), .in2(register_3_q), .in3(register_4_q), .in4(register_5_q),
    .in5(register_6_q), .in6(register_7_q), .in7(register_8_q), .in8(register_9_q), .in9(register_10_q),
    .in10(register_11_q), .in11(register_12_q), .in12(register_13_q), .in13(register_14_q),
    .in14(register_15_q), .in15(register_16_q), .in16(register_17_q), .in17(register_18_q),
    .in18(register_19_q), .in19(register_20_q), .in20(register_21_q), .in21(register_22_q),
    .in22(register_23_q), .in23(register_24_q), .in24(register_25_q), .in25(register_26_q),
    .in26(register_27_q), .in27(register_28_q), .in28(register_29_q), .in29(register_30_q),
    .in30(register_31_q), .in31(register_32_q), .out(multiplexer_1_out), .sel(Read_Reg_1[4:0]));  // open: en
  Multiplexer #(.select(5), .width(26)) multiplexer_2 (
    .in0(register_33_q), .in1(register_34_q), .in2(register_35_q), .in3(register_36_q), .in4(register_37_q),
    .in5(register_38_q), .in6(register_39_q), .in7(register_40_q), .in8(register_41_q), .in9(register_42_q),
    .in10(register_43_q), .in11(register_44_q), .in12(register_45_q), .in13(register_46_q),
    .in14(register_47_q), .in15(register_48_q), .in16(register_49_q), .in17(register_50_q),
    .in18(register_51_q), .in19(register_52_q), .in20(register_53_q), .in21(register_54_q),
    .in22(register_55_q), .in23(register_56_q), .in24(register_57_q), .in25(register_58_q),
    .in26(register_59_q), .in27(register_60_q), .in28(register_61_q), .in29(register_62_q),
    .in30(register_63_q), .in31(register_64_q), .out(multiplexer_2_out), .sel(Read_Reg_1[4:0]));  // open: en
  Multiplexer #(.select(5), .width(26)) multiplexer_3 (
    .in0(register_1_q), .in1(register_2_q), .in2(register_3_q), .in3(register_4_q), .in4(register_5_q),
    .in5(register_6_q), .in6(register_7_q), .in7(register_8_q), .in8(register_9_q), .in9(register_10_q),
    .in10(register_11_q), .in11(register_12_q), .in12(register_13_q), .in13(register_14_q),
    .in14(register_15_q), .in15(register_16_q), .in16(register_17_q), .in17(register_18_q),
    .in18(register_19_q), .in19(register_20_q), .in20(register_21_q), .in21(register_22_q),
    .in22(register_23_q), .in23(register_24_q), .in24(register_25_q), .in25(register_26_q),
    .in26(register_27_q), .in27(register_28_q), .in28(register_29_q), .in29(register_30_q),
    .in30(register_31_q), .in31(register_32_q), .out(multiplexer_3_out), .sel(Read_Reg_2[4:0]));  // open: en
  Multiplexer #(.select(5), .width(26)) multiplexer_4 (
    .in0(register_33_q), .in1(register_34_q), .in2(register_35_q), .in3(register_36_q), .in4(register_37_q),
    .in5(register_38_q), .in6(register_39_q), .in7(register_40_q), .in8(register_41_q), .in9(register_42_q),
    .in10(register_43_q), .in11(register_44_q), .in12(register_45_q), .in13(register_46_q),
    .in14(register_47_q), .in15(register_48_q), .in16(register_49_q), .in17(register_50_q),
    .in18(register_51_q), .in19(register_52_q), .in20(register_53_q), .in21(register_54_q),
    .in22(register_55_q), .in23(register_56_q), .in24(register_57_q), .in25(register_58_q),
    .in26(register_59_q), .in27(register_60_q), .in28(register_61_q), .in29(register_62_q),
    .in30(register_63_q), .in31(register_64_q), .out(multiplexer_4_out), .sel(Read_Reg_2[4:0]));  // open: en
  Multiplexer #(.width(26)) multiplexer_5 (
    .in0(multiplexer_1_out), .in1(multiplexer_2_out), .out(Read_Data_1), .sel(Read_Reg_1[5]));  // open: en
  Multiplexer #(.width(26)) multiplexer_6 (
    .in0(multiplexer_3_out), .in1(multiplexer_4_out), .out(Read_Data_2), .sel(Read_Reg_2[5]));  // open: en
endmodule

module One_bit_ALU (
  input  A,
  input  B,
  input  Lshift,
  input  Rshift,
  input  Cin,
  input  B_invert,
  input  [2:0] Select,
  output S,
  output Cout
);

  wire adder_1_out, and_1_out, and_2_out, nor_1_out, or_1_out, xor_1_out, xor_2_out;

  xor xor_1 (xor_1_out, B, and_2_out);
  and and_1 (and_1_out, A, B);
  or or_1 (or_1_out, A, B);
  xor xor_2 (xor_2_out, A, B);
  nor nor_1 (nor_1_out, A, B);
  Adder #(.width(1)) adder_1 (.a(A), .b(xor_1_out), .out(adder_1_out), .cin(Cin), .cout(Cout));
  and and_2 (and_2_out, Select[0], B_invert);
  Multiplexer #(.select(3)) multiplexer_1 (
    .in0(and_1_out), .in1(or_1_out), .in2(adder_1_out), .in3(adder_1_out), .in4(xor_2_out), .in5(nor_1_out),
    .in6(Lshift), .in7(Rshift), .out(S), .sel(Select));  // open: en
endmodule

module _26_bit_ALU (
  input  [25:0] A,
  input  [25:0] B,
  input  Cin,
  input  Binv,
  input  [2:0] Select,
  output ZeroFlag,
  output [25:0] Output,
  output Cout,
  output OverFlow_Flag
);

  wire one_bit_alu_1_cout, one_bit_alu_2_cout, one_bit_alu_3_cout, one_bit_alu_4_cout, one_bit_alu_5_cout,
       one_bit_alu_6_cout, one_bit_alu_7_cout, one_bit_alu_8_cout, one_bit_alu_9_cout, one_bit_alu_10_cout,
       one_bit_alu_11_cout, one_bit_alu_12_cout, one_bit_alu_13_cout, one_bit_alu_14_cout,
       one_bit_alu_15_cout, one_bit_alu_16_cout, one_bit_alu_17_cout, one_bit_alu_18_cout,
       one_bit_alu_19_cout, one_bit_alu_20_cout, one_bit_alu_21_cout, one_bit_alu_22_cout,
       one_bit_alu_23_cout, one_bit_alu_24_cout, one_bit_alu_25_cout;

  One_bit_ALU one_bit_alu_1 (
    .S(Output[0]), .Cout(one_bit_alu_1_cout), .B_invert(Binv), .A(A[0]), .B(B[0]), .Cin(Cin),
    .Select(Select), .Lshift(1'b0), .Rshift(A[1]));
  One_bit_ALU one_bit_alu_2 (
    .S(Output[1]), .Cout(one_bit_alu_2_cout), .B_invert(Binv), .A(A[1]), .B(B[1]), .Cin(one_bit_alu_1_cout),
    .Select(Select), .Lshift(A[0]), .Rshift(A[2]));
  One_bit_ALU one_bit_alu_3 (
    .S(Output[2]), .Cout(one_bit_alu_3_cout), .B_invert(Binv), .A(A[2]), .B(B[2]), .Cin(one_bit_alu_2_cout),
    .Select(Select), .Lshift(A[1]), .Rshift(A[3]));
  One_bit_ALU one_bit_alu_4 (
    .S(Output[3]), .Cout(one_bit_alu_4_cout), .B_invert(Binv), .A(A[3]), .B(B[3]), .Cin(one_bit_alu_3_cout),
    .Select(Select), .Lshift(A[2]), .Rshift(A[4]));
  One_bit_ALU one_bit_alu_5 (
    .S(Output[4]), .Cout(one_bit_alu_5_cout), .B_invert(Binv), .A(A[4]), .B(B[4]), .Cin(one_bit_alu_4_cout),
    .Select(Select), .Lshift(A[3]), .Rshift(A[5]));
  One_bit_ALU one_bit_alu_6 (
    .S(Output[5]), .Cout(one_bit_alu_6_cout), .B_invert(Binv), .A(A[5]), .B(B[5]), .Cin(one_bit_alu_5_cout),
    .Select(Select), .Lshift(A[4]), .Rshift(A[6]));
  One_bit_ALU one_bit_alu_7 (
    .S(Output[6]), .Cout(one_bit_alu_7_cout), .B_invert(Binv), .A(A[6]), .B(B[6]), .Cin(one_bit_alu_6_cout),
    .Select(Select), .Lshift(A[5]), .Rshift(A[7]));
  One_bit_ALU one_bit_alu_8 (
    .S(Output[7]), .Cout(one_bit_alu_8_cout), .B_invert(Binv), .A(A[7]), .B(B[7]), .Cin(one_bit_alu_7_cout),
    .Select(Select), .Lshift(A[6]), .Rshift(A[8]));
  One_bit_ALU one_bit_alu_9 (
    .S(Output[8]), .Cout(one_bit_alu_9_cout), .B_invert(Binv), .A(A[8]), .B(B[8]), .Cin(one_bit_alu_8_cout),
    .Select(Select), .Lshift(A[7]), .Rshift(A[9]));
  One_bit_ALU one_bit_alu_10 (
    .S(Output[9]), .Cout(one_bit_alu_10_cout), .B_invert(Binv), .A(A[9]), .B(B[9]), .Cin(one_bit_alu_9_cout),
    .Select(Select), .Lshift(A[8]), .Rshift(A[10]));
  One_bit_ALU one_bit_alu_11 (
    .S(Output[10]), .Cout(one_bit_alu_11_cout), .B_invert(Binv), .A(A[10]), .B(B[10]),
    .Cin(one_bit_alu_10_cout), .Select(Select), .Lshift(A[9]), .Rshift(A[11]));
  One_bit_ALU one_bit_alu_12 (
    .S(Output[11]), .Cout(one_bit_alu_12_cout), .B_invert(Binv), .A(A[11]), .B(B[11]),
    .Cin(one_bit_alu_11_cout), .Select(Select), .Lshift(A[10]), .Rshift(A[12]));
  One_bit_ALU one_bit_alu_13 (
    .S(Output[12]), .Cout(one_bit_alu_13_cout), .B_invert(Binv), .A(A[12]), .B(B[12]),
    .Cin(one_bit_alu_12_cout), .Select(Select), .Lshift(A[11]), .Rshift(A[13]));
  One_bit_ALU one_bit_alu_14 (
    .S(Output[13]), .Cout(one_bit_alu_14_cout), .B_invert(Binv), .A(A[13]), .B(B[13]),
    .Cin(one_bit_alu_13_cout), .Select(Select), .Lshift(A[12]), .Rshift(A[14]));
  One_bit_ALU one_bit_alu_15 (
    .S(Output[14]), .Cout(one_bit_alu_15_cout), .B_invert(Binv), .A(A[14]), .B(B[14]),
    .Cin(one_bit_alu_14_cout), .Select(Select), .Lshift(A[13]), .Rshift(A[15]));
  One_bit_ALU one_bit_alu_16 (
    .S(Output[15]), .Cout(one_bit_alu_16_cout), .B_invert(Binv), .A(A[15]), .B(B[15]),
    .Cin(one_bit_alu_15_cout), .Select(Select), .Lshift(A[14]), .Rshift(A[16]));
  One_bit_ALU one_bit_alu_17 (
    .S(Output[16]), .Cout(one_bit_alu_17_cout), .B_invert(Binv), .A(A[16]), .B(B[16]),
    .Cin(one_bit_alu_16_cout), .Select(Select), .Lshift(A[15]), .Rshift(A[17]));
  One_bit_ALU one_bit_alu_18 (
    .S(Output[17]), .Cout(one_bit_alu_18_cout), .B_invert(Binv), .A(A[17]), .B(B[17]),
    .Cin(one_bit_alu_17_cout), .Select(Select), .Lshift(A[16]), .Rshift(A[18]));
  One_bit_ALU one_bit_alu_19 (
    .S(Output[18]), .Cout(one_bit_alu_19_cout), .B_invert(Binv), .A(A[18]), .B(B[18]),
    .Cin(one_bit_alu_18_cout), .Select(Select), .Lshift(A[17]), .Rshift(A[19]));
  One_bit_ALU one_bit_alu_20 (
    .S(Output[19]), .Cout(one_bit_alu_20_cout), .B_invert(Binv), .A(A[19]), .B(B[19]),
    .Cin(one_bit_alu_19_cout), .Select(Select), .Lshift(A[18]), .Rshift(A[20]));
  One_bit_ALU one_bit_alu_21 (
    .S(Output[20]), .Cout(one_bit_alu_21_cout), .B_invert(Binv), .A(A[20]), .B(B[20]),
    .Cin(one_bit_alu_20_cout), .Select(Select), .Lshift(A[19]), .Rshift(A[21]));
  One_bit_ALU one_bit_alu_22 (
    .S(Output[21]), .Cout(one_bit_alu_22_cout), .B_invert(Binv), .A(A[21]), .B(B[21]),
    .Cin(one_bit_alu_21_cout), .Select(Select), .Lshift(A[20]), .Rshift(A[22]));
  One_bit_ALU one_bit_alu_23 (
    .S(Output[22]), .Cout(one_bit_alu_23_cout), .B_invert(Binv), .A(A[22]), .B(B[22]),
    .Cin(one_bit_alu_22_cout), .Select(Select), .Lshift(A[21]), .Rshift(A[23]));
  One_bit_ALU one_bit_alu_24 (
    .S(Output[23]), .Cout(one_bit_alu_24_cout), .B_invert(Binv), .A(A[23]), .B(B[23]),
    .Cin(one_bit_alu_23_cout), .Select(Select), .Lshift(A[22]), .Rshift(A[24]));
  One_bit_ALU one_bit_alu_25 (
    .S(Output[24]), .Cout(one_bit_alu_25_cout), .B_invert(Binv), .A(A[24]), .B(B[24]),
    .Cin(one_bit_alu_24_cout), .Select(Select), .Lshift(A[23]), .Rshift(A[25]));
  One_bit_ALU one_bit_alu_26 (
    .S(Output[25]), .Cout(Cout), .B_invert(Binv), .A(A[25]), .B(B[25]), .Cin(one_bit_alu_25_cout),
    .Select(Select), .Lshift(A[24]), .Rshift(1'b0));
  nor nor_1 (ZeroFlag, Output[0], Output[1], Output[2], Output[3], Output[4], Output[5], Output[6], Output[7], Output[8], Output[9], Output[10], Output[11], Output[12], Output[13], Output[14], Output[15], Output[16], Output[17], Output[18], Output[19], Output[20], Output[21], Output[22], Output[23], Output[24], Output[25]);
  xor xor_1 (OverFlow_Flag, one_bit_alu_25_cout, Cout);
  // AND_Gate and_1 is placed but not wired
endmodule

module Control_Unit (
  input  [4:0] OPcode,
  output MemWrite,
  output MemToReg___MemRead,
  output RegWrite,
  output Regdst,
  output Jump,
  output ALUsrc,
  output Branch,
  output BNE,
  output ExtOp,
  output [2:0] ALUop
);

  wire decoder_1_out0, decoder_1_out1, decoder_1_out2, decoder_1_out3, decoder_1_out6, decoder_1_out7,
       decoder_1_out8, decoder_1_out9, decoder_1_out10, decoder_1_out11, decoder_1_out12, decoder_1_out13,
       decoder_1_out15;

  Decoder #(.select(5)) decoder_1 (
    .out0(decoder_1_out0), .out1(decoder_1_out1), .out2(decoder_1_out2), .out3(decoder_1_out3),
    .out4(MemToReg___MemRead), .out5(MemWrite), .out6(decoder_1_out6), .out7(decoder_1_out7),
    .out8(decoder_1_out8), .out9(decoder_1_out9), .out10(decoder_1_out10), .out11(decoder_1_out11),
    .out12(decoder_1_out12), .out13(decoder_1_out13), .out14(Jump), .out15(decoder_1_out15), .out16(BNE),
    .sel(OPcode));  // open: out17, out18, out19, out20, out21, out22, out23, out24, out25, out26, out27, out28, out29, out30, out31, en
  or or_1 (ALUop[0], decoder_1_out1, decoder_1_out7, decoder_1_out3, decoder_1_out9, decoder_1_out11, decoder_1_out13, decoder_1_out15, BNE);
  or or_2 (ALUop[1], decoder_1_out2, decoder_1_out6, decoder_1_out3, decoder_1_out7, MemToReg___MemRead, MemWrite, decoder_1_out12, decoder_1_out13, decoder_1_out15, BNE);
  or or_3 (ALUop[2], decoder_1_out0, decoder_1_out1, decoder_1_out12, decoder_1_out13);
  or or_4 (RegWrite, decoder_1_out0, decoder_1_out1, decoder_1_out2, decoder_1_out3, MemToReg___MemRead, decoder_1_out6, decoder_1_out7, decoder_1_out8, decoder_1_out9, decoder_1_out10, decoder_1_out11, decoder_1_out12, decoder_1_out13);
  or or_5 (Regdst, decoder_1_out2, decoder_1_out3, decoder_1_out0, decoder_1_out1, decoder_1_out8, decoder_1_out9, decoder_1_out12, decoder_1_out13);
  or or_6 (ALUsrc, decoder_1_out7, decoder_1_out6, decoder_1_out10, decoder_1_out11, MemWrite, MemToReg___MemRead);
  or or_7 (Branch, decoder_1_out15, BNE);
  or or_8 (ExtOp, decoder_1_out10, decoder_1_out11);

  // Notes on the sheet:
  //   BNE
  //   XOR
  //   NOR
  //   J
  //   BEQ
  //   ADD
  //   SLL
  //   SRL
  //   SUB
  //   ORI
  //   LW
  //   ANDI
  //   SW
  //   OR
  //   ADDI
  //   AND
  //   SUBI
  //   ALUOp (bit 0)
  //   ALUOp (bit 1)
  //   ALUOp (bit 2)
  //   BNE
endmodule

module Combined_Circuit (
  input  in_1,
  input  [15:0] LI,
  output [7:0] out_3,
  output [7:0] out_4,
  output [7:0] out_5,
  output [7:0] out_6,
  output [25:0] ALU_Output,
  output [5:0] RT,
  output [5:0] RS,
  output [5:0] RD,
  output [25:0] RS_2,
  output [25:0] RT__IM,
  output [22:0] out_13,
  output out_14,
  output out_15,
  output [25:0] WD,
  output [25:0] Only_RT
);

  wire alu_control_unit_1_binv, alu_control_unit_1_cin, and_1_out, clock_1_out, control_unit_1_alusrc,
       control_unit_1_bne, control_unit_1_branch, control_unit_1_extop, control_unit_1_jump,
       control_unit_1_memtoreg___memread, control_unit_1_memwrite, control_unit_1_regdst,
       control_unit_1_regwrite, n26_bit_alu_1_zeroflag, xor_1_out;
  wire [2:0] alu_control_unit_1_select, control_unit_1_aluop;
  wire [7:0] multiplexer_3_out;
  wire [25:0] bit_extender_1_out, ram_1_data;

  Clock clock_1 (.out(clock_1_out));
  Register PC (.D(out_6), .Q(out_5), .clk(clock_1_out), .clr(in_1));  // open: en
  Adder adder_1 (.a(out_5), .b(8'h1), .out(out_4));  // open: cin, cout
  ROM #(.dataWidth(23)) rom_1 (.addr(out_5), .data(out_13));  // open: sel
  ALU_Control_Unit alu_control_unit_1 (
    .Select(alu_control_unit_1_select), .Binv(alu_control_unit_1_binv), .Cin(alu_control_unit_1_cin),
    .ALUop__3_bits(control_unit_1_aluop));
  Multiplexer #(.width(6)) multiplexer_1 (
    .in0(out_13[5:0]), .in1(out_13[11:6]), .out(RD), .sel(control_unit_1_regdst));  // open: en
  assign bit_extender_1_out = {{20{control_unit_1_extop}}, out_13[5:0]};  // Bit_Extender bit_extender_1
  Control_Unit control_unit_1 (
    .ALUop(control_unit_1_aluop), .RegWrite(control_unit_1_regwrite), .Regdst(control_unit_1_regdst),
    .Jump(control_unit_1_jump), .Branch(control_unit_1_branch),
    .MemToReg___MemRead(control_unit_1_memtoreg___memread), .MemWrite(control_unit_1_memwrite),
    .OPcode(out_13[22:18]), .ALUsrc(control_unit_1_alusrc), .ExtOp(control_unit_1_extop),
    .BNE(control_unit_1_bne));
  REG_FILE reg_file_1 (
    .Read_Reg_1(out_13[17:12]), .Right_Reg_RD(RD), .Write_Data(WD), .Read_Data_1(RS_2),
    .Read_Data_2(Only_RT), .Read_Reg_2(out_13[11:6]), .CLK(clock_1_out),
    .Write_Control(control_unit_1_regwrite));
  Multiplexer #(.width(26)) multiplexer_2 (
    .in0(Only_RT), .in1(bit_extender_1_out), .out(RT__IM), .sel(control_unit_1_alusrc));  // open: en
  xor xor_1 (xor_1_out, control_unit_1_bne, n26_bit_alu_1_zeroflag);
  Adder adder_2 (.a(out_4), .b(bit_extender_1_out[7:0]), .out(out_3));  // open: cin, cout
  _26_bit_ALU u_26_bit_alu_1 (
    .Output(ALU_Output), .Cout(out_15), .OverFlow_Flag(out_14), .Cin(alu_control_unit_1_cin),
    .Select(alu_control_unit_1_select), .Binv(alu_control_unit_1_binv), .ZeroFlag(n26_bit_alu_1_zeroflag),
    .A(RS_2), .B(RT__IM));
  and and_1 (and_1_out, control_unit_1_branch, xor_1_out);
  Multiplexer #(.width(8)) multiplexer_3 (
    .in0(out_4), .in1(out_3), .out(multiplexer_3_out), .sel(and_1_out));  // open: en
  Multiplexer #(.width(8)) multiplexer_4 (
    .in0(multiplexer_3_out), .in1(out_13[7:0]), .out(out_6), .sel(control_unit_1_jump));  // open: en
  RAM #(.addrWidth(9), .dataWidth(26), .bus("separate")) ram_1 (
    .addr(ALU_Output[8:0]), .din(Only_RT), .data(ram_1_data), .str(control_unit_1_memwrite),
    .clk(clock_1_out), .ld(control_unit_1_memtoreg___memread));  // open: sel, clr
  Multiplexer #(.width(26)) multiplexer_5 (
    .in0(ALU_Output), .in1(ram_1_data), .out(WD), .sel(control_unit_1_memtoreg___memread));  // open: en

  assign RS = out_13[17:12];
  assign RT = out_13[11:6];

  // Notes on the sheet:
  //   Instruction Memory
  //   PC+1
  //   contents of rom_1 (hex, n*v repeats v):
  //   1 40002 80003 c0004 10064f 140140 18018a 1c01c5 200008 240009 28028f 2c02c3 30000c 34000d 38000f
  //   3c0010 400011 80000
  //   RS
  //   OPcode
  //   RT
  //   RD
  //   RD/RT MUX
  //   ExtImmOP
  //   Load Immediate (26)
  //   RT/IM MUX
  //   BNE signal
  //   ZeroFlag
  //   Jump Target Address (8 bit)
  //   PC+1 Address
  //   Branch control
  //   Target Address
  //   Branch MUX
  //   Jump MUX
  //   Jump Control
  //   Data Memory
  //   STR
  //   LD
  //   Read/Write MUX
endmodule

module ALU_Control_Unit (
  input  [2:0] ALUop__3_bits,
  output [2:0] Select,
  output Binv,
  output Cin
);

  wire not_1_out;

  not not_1 (not_1_out, ALUop__3_bits[2]);
  and and_1 (Binv, ALUop__3_bits[0], ALUop__3_bits[1], not_1_out);

  assign Cin = Binv;
  assign Select = ALUop__3_bits;

  // Notes on the sheet:
  //   ALUOp (bit 0)
  //   ALUOp (bit 1)
  //   ALUop (bit 2)
endmodule
